# Fritzing sketch scheme (saved by Fritzing 1.0.2b)

parts:
  Mod1 = Raspberry Pi 4B
  Part1 = Skystars h743
  Part1_MAIN1 = Skystars h743  # not connected
  Part1_CN2 = Skystars h743  # not connected
  Part1_CN9 = Skystars h743  # not connected
  Part1_CN6 = Skystars h743  # not connected
  Part2 = Skystars h743
  Part2_MAIN1 = Skystars h743  # not connected
  Part2_CN2 = Skystars h743  # not connected
  Part2_CN9 = Skystars h743  # not connected
  Part2_CN6 = Skystars h743  # not connected
  ORP_Circuit1 = ORP Circuit
  U1 = Relay [package=rf-link_tx]
  M2 = BMP280
  Walksnail1 = Walksnail GPS
  Walksnail2 = Walksnail GPS
  Part3 = Skystars h743 km60a
  Part3_MAIN1 = Skystars h743 km60a  # not connected
  Part3_CN2 = Skystars h743 km60a  # not connected
  Part3_CN9 = Skystars h743 km60a  # not connected
  Part3_CN6 = Skystars h743 km60a  # not connected
  U2 = buzzer [package="buzzer module"]
  J1 = Piezo Speaker
  SERVO1 = Adafruit Feedback Servo (small)
  Motor_FPV1 = Motor
  Motor_FPV2 = Motor
  Motor_FPV3 = Motor
  Motor_FPV4 = Motor
  J2 = XT60 Connector [package=THT]
  SCW05B-1 = SCW05B-05
  SCW05B-2 = SCW05B-05
  MH-ET_LIVE_ESP32_DEVKIT1 = MH-ET LIVE ESP32 DEVKIT 38 pins
  Part5 = FTDI Basic Programmer

nets:
  5V: Mod1.5V, Walksnail2.5V, SCW05B-2.Vout_+
  N1: Mod1.GPIO2, M2.SDA
  N2: Mod1.GPIO3, M2.SCL
  GND: Mod1.GND, M2.GND, Walksnail2.GND, SCW05B-2.GND, Part5.GND
  N3: Mod1.GPIO4, Walksnail2.RX
  N4: Mod1.GPIO14, Part5.RXI
  N5: Mod1.GPIO15, Part5.TXO
  N6: Mod1.GPIO27, ORP_Circuit1.Triger1
  N7: Mod1.GPIO22, ORP_Circuit1.Triger2
  N8: Mod1.ID_SD, Part1.connector6
  N9: Mod1.ID_SC, Part1.connector5
  N10: Mod1.GPIO5, Walksnail2.TX
  N11: Mod1.GPIO20, U2.Trigger
  N12: Mod1.GPIO21, U1.Teiger
  N13: Part1.connector1, MH-ET_LIVE_ESP32_DEVKIT1.IO17
  N14: Part1.connector2, MH-ET_LIVE_ESP32_DEVKIT1.GND
  N15: Part1.connector3, MH-ET_LIVE_ESP32_DEVKIT1.IO16
  N16: Part1.connector4, MH-ET_LIVE_ESP32_DEVKIT1.5V
  N17: Part1.connector10, Part1.connector24, ORP_Circuit1.VCC_BAT_+#2
  N18: Part1.connector11, Part1.connector16, Part1.connector30, Walksnail1.GND, Walksnail1.SCL, Part3.connector22
  N19: Part1.connector12, Walksnail1.SDA
  N20: Part1.connector15, Walksnail1.5V
  N21: Part1.connector17, Walksnail1.RX
  N22: Part1.connector18, Walksnail1.TX
  N23: Part1.connector23, ORP_Circuit1.GND#8
  N24: Part1.connector25, Part3.connector17
  N25: Part1.connector27, Part3.connector19
  N26: Part1.connector28, Part3.connector20
  N27: Part1.connector29, Part3.connector21
  N28: Part2.connector10, SERVO1.Signal
  N29: ORP_Circuit1.VCC_BAT_+#0, J2.VCC
  N30: ORP_Circuit1.GND#1, J2.GND
  N31: ORP_Circuit1.VCC_BAT_+#3, SCW05B-2.Vin_+
  N32: ORP_Circuit1.VCC_BAT_+#4, SCW05B-1.Vin_+
  N33: ORP_Circuit1.GND#7, SCW05B-1.Vin_-, SCW05B-2.Vin_-
  N34: ORP_Circuit1.GND#9, Part3.connector1
  N35: ORP_Circuit1.OUT_VCC, Part3.connector2
  N36: U1.GND#0, U2.GND
  N37: U1.GND#1, SCW05B-1.GND
  N38: U1.+5V#3, SCW05B-1.Vout_+
  N39: U1.Gnd, SERVO1.Ground
  N40: U1.+5V#7, U2.+5V
  N41: U1.Out_5V, SERVO1.Power
  N42: Part3.connector3, Motor_FPV4.S3
  N43: Part3.connector4, Motor_FPV4.S2
  N44: Part3.connector5, Motor_FPV4.S1
  N45: Part3.connector6, Motor_FPV3.S3
  N46: Part3.connector7, Motor_FPV3.S2
  N47: Part3.connector8, Motor_FPV3.S1
  N48: Part3.connector9, Motor_FPV2.S1
  N49: Part3.connector10, Motor_FPV2.S2
  N50: Part3.connector11, Motor_FPV2.S3
  N51: Part3.connector12, Motor_FPV1.S1
  N52: Part3.connector13, Motor_FPV1.S2
  N53: Part3.connector14, Motor_FPV1.S3
  N54: U2.out+, J1.pin1
  N55: U2.out-, J1.pin2

custom parts:
  Relay: RF Link transmitters WRL-8945, 8946
  BMP280: Temperature Humidity Barometric presure Sensor
  Adafruit Feedback Servo (small): Adafruit Feedback Servo (Small)
  XT60 Connector: Yellow XT60 connector for high current loads up to 40A
  MH-ET LIVE ESP32 DEVKIT 38 pins: http://mh.nodebb.com/topic/2/mh-et-live-esp32-devkit
